// Logisim project 直接相连映射方式cache电路.circ as structural Verilog: 8 circuits, main circuit cache（直接相联映射）电路（4个cache块）
// 直接相联cache
module \cache_直接相联映射_电路_4个cache块  (
  input  [15:0] Addr,
  input  [31:0] BlockDataIn,
  input  BlkDataReady,
  input  CLK,
  output Miss,
  output [7:0] DataOut
);

  wire and_2_out, and_3_out, and_4_out, and_5_out, comparator_1_eq, Hit, L0, L1, L2, L3, Valid, VALID_2_q,
       VALID_3_q, VALID_4_q, VALID_q;
  wire [11:0] TAG_2_q, TAG_3_q, TAG_4_q, TAG_q, TagData;
  wire [31:0] DATA_COPY_2_q, DATA_COPY_3_q, DATA_COPY_q, SlotData, \数据块副本_q ;

  Register #(.width(1), .trigger("rising"), .Select("low")) u_VALID (
    .D(1'b1), .en(and_2_out), .Q(VALID_q), .clk(CLK));  // open: clr
  Register #(.width(1), .trigger("rising"), .Select("low")) VALID_2 (
    .D(1'b1), .en(and_3_out), .Q(VALID_2_q), .clk(CLK));  // open: clr
  Register #(.width(1), .trigger("rising"), .Select("low")) VALID_3 (
    .D(1'b1), .en(and_4_out), .Q(VALID_3_q), .clk(CLK));  // open: clr
  Register #(.width(1), .trigger("rising"), .Select("low")) VALID_4 (
    .D(1'b1), .en(and_5_out), .Q(VALID_4_q), .clk(CLK));  // open: clr
  Multiplexer #(.select(2), .width(8), .disabled("Z"), .enable("true")) multiplexer_1 (
    .in0(SlotData[7:0]), .in1(SlotData[15:8]), .in2(SlotData[23:16]), .in3(SlotData[31:24]), .out(DataOut),
    .sel(Addr[1:0]), .en(Hit));
  assign Valid = L0 ? VALID_q : 1'bz;  // Controlled_Buffer controlled_buffer_1
  assign Valid = L1 ? VALID_2_q : 1'bz;  // Controlled_Buffer controlled_buffer_2
  assign Valid = L2 ? VALID_3_q : 1'bz;  // Controlled_Buffer controlled_buffer_3
  assign Valid = L3 ? VALID_4_q : 1'bz;  // Controlled_Buffer controlled_buffer_4
  Decoder #(.select(2), .tristate("false"), .disabled(0), .enable("false")) decoder_1 (
    .out0(L0), .out1(L1), .out2(L2), .out3(L3), .sel(Addr[3:2]));
  Register #(.width(12), .trigger("rising"), .Select("low")) TAG (
    .D(Addr[15:4]), .en(and_2_out), .Q(TAG_q), .clk(CLK));  // open: clr
  assign TagData = L0 ? TAG_q : 12'bz;  // Controlled_Buffer controlled_buffer_5
  Register #(.width(12), .trigger("rising"), .Select("low")) TAG_2 (
    .D(Addr[15:4]), .en(and_3_out), .Q(TAG_2_q), .clk(CLK));  // open: clr
  assign TagData = L1 ? TAG_2_q : 12'bz;  // Controlled_Buffer controlled_buffer_6
  Register #(.width(12), .trigger("rising"), .Select("low")) TAG_3 (
    .D(Addr[15:4]), .en(and_4_out), .Q(TAG_3_q), .clk(CLK));  // open: clr
  assign TagData = L2 ? TAG_3_q : 12'bz;  // Controlled_Buffer controlled_buffer_7
  Register #(.width(12), .trigger("rising"), .Select("low")) TAG_4 (
    .D(Addr[15:4]), .en(and_5_out), .Q(TAG_4_q), .clk(CLK));  // open: clr
  assign TagData = L3 ? TAG_4_q : 12'bz;  // Controlled_Buffer controlled_buffer_8
  Comparator #(.width(12), .mode("twosComplement")) comparator_1 (
    .a(Addr[15:4]), .b(TagData), .eq(comparator_1_eq));  // open: gt, lt
  Register #(.width(32), .trigger("rising"), .Select("low")) \u_数据块副本  (
    .D(BlockDataIn), .en(and_2_out), .Q(\数据块副本_q ), .clk(CLK));  // open: clr
  Register #(.width(32), .trigger("rising"), .Select("low")) DATA_COPY (
    .D(BlockDataIn), .en(and_3_out), .Q(DATA_COPY_q), .clk(CLK));  // open: clr
  Register #(.width(32), .trigger("rising"), .Select("low")) DATA_COPY_2 (
    .D(BlockDataIn), .en(and_4_out), .Q(DATA_COPY_2_q), .clk(CLK));  // open: clr
  Register #(.width(32), .trigger("rising"), .Select("low")) DATA_COPY_3 (
    .D(BlockDataIn), .en(and_5_out), .Q(DATA_COPY_3_q), .clk(CLK));  // open: clr
  not not_1 (Miss, Hit);
  and and_1 (Hit, comparator_1_eq, Valid);
  assign SlotData = L0 ? \数据块副本_q  : 32'bz;  // Controlled_Buffer controlled_buffer_9
  assign SlotData = L1 ? DATA_COPY_q : 32'bz;  // Controlled_Buffer controlled_buffer_10
  assign SlotData = L2 ? DATA_COPY_2_q : 32'bz;  // Controlled_Buffer controlled_buffer_11
  assign SlotData = L3 ? DATA_COPY_3_q : 32'bz;  // Controlled_Buffer controlled_buffer_12
  and and_2 (and_2_out, L0, BlkDataReady);
  and and_3 (and_3_out, L1, BlkDataReady);
  and and_4 (and_4_out, L2, BlkDataReady);
  and and_5 (and_5_out, L3, BlkDataReady);

  // Other names for the same wires on the sheet: Blk[31:0] = BlockDataIn; BlkReady = BlkDataReady;
  //   Offset[1:0] = Addr[1:0]; 字节地址[15:0] = Addr; Index[1:0] = Addr[3:2]; Tag[11:0] = Addr[15:4]

  // Notes on the sheet:
  //   输入引脚区
  //   有效位
  //   三态门控制多行输出
  //   行选中
  //   标记位
  //   cache（直接相联映射）电路（4个cache块）
  //   块数据输出
  //   输出引脚区
endmodule

// 直接相联cache
module \cache_直接相联映射_电路_16个cache块  (
  input  [15:0] Addr,
  input  [31:0] BlockDataIn,
  input  BlkDataReady,
  input  CLK,
  output Miss,
  output [7:0] DataOut
);

  wire and_2_out, and_3_out, and_4_out, and_5_out, and_6_out, and_7_out, and_8_out, and_9_out, and_10_out,
       and_11_out, and_12_out, and_13_out, and_14_out, and_15_out, and_16_out, and_17_out, comparator_1_eq,
       Hit, L0, L1, L2, L3, L4, L5, L6, L7, L8, L9, L10, L11, L12, L13, L14, L15, Valid, VALID_2_q,
       VALID_3_q, VALID_4_q, VALID_5_q, VALID_6_q, VALID_7_q, VALID_8_q, VALID_9_q, VALID_10_q, VALID_11_q,
       VALID_12_q, VALID_13_q, VALID_14_q, VALID_15_q, VALID_16_q, VALID_q;
  wire [9:0] TAG_2_q, TAG_3_q, TAG_4_q, TAG_5_q, TAG_6_q, TAG_7_q, TAG_8_q, TAG_9_q, TAG_10_q, TAG_11_q,
       TAG_12_q, TAG_13_q, TAG_14_q, TAG_15_q, TAG_16_q, TAG_q, TagData;
  wire [31:0] DATA_COPY_2_q, DATA_COPY_3_q, DATA_COPY_4_q, DATA_COPY_5_q, DATA_COPY_6_q, DATA_COPY_7_q,
       DATA_COPY_8_q, DATA_COPY_9_q, DATA_COPY_10_q, DATA_COPY_11_q, DATA_COPY_12_q, DATA_COPY_13_q,
       DATA_COPY_14_q, DATA_COPY_q, SlotData, \数据块副本_2_q , \数据块副本_q ;

  Register #(.width(1), .trigger("rising"), .Select("low")) u_VALID (
    .D(1'b1), .en(and_2_out), .Q(VALID_q), .clk(CLK));  // open: clr
  Register #(.width(1), .trigger("rising"), .Select("low")) VALID_2 (
    .D(1'b1), .en(and_3_out), .Q(VALID_2_q), .clk(CLK));  // open: clr
  Register #(.width(1), .trigger("rising"), .Select("low")) VALID_3 (
    .D(1'b1), .en(and_4_out), .Q(VALID_3_q), .clk(CLK));  // open: clr
  Register #(.width(1), .trigger("rising"), .Select("low")) VALID_4 (
    .D(1'b1), .en(and_5_out), .Q(VALID_4_q), .clk(CLK));  // open: clr
  Register #(.width(1), .trigger("rising"), .Select("low")) VALID_5 (
    .D(1'b1), .en(and_6_out), .Q(VALID_5_q), .clk(CLK));  // open: clr
  Register #(.width(1), .trigger("rising"), .Select("low")) VALID_6 (
    .D(1'b1), .en(and_7_out), .Q(VALID_6_q), .clk(CLK));  // open: clr
  Register #(.width(1), .trigger("rising"), .Select("low")) VALID_7 (
    .D(1'b1), .en(and_8_out), .Q(VALID_7_q), .clk(CLK));  // open: clr
  Register #(.width(1), .trigger("rising"), .Select("low")) VALID_8 (
    .D(1'b1), .en(and_9_out), .Q(VALID_8_q), .clk(CLK));  // open: clr
  Multiplexer #(.select(2), .width(8), .disabled("Z"), .enable("true")) multiplexer_1 (
    .in0(SlotData[7:0]), .in1(SlotData[15:8]), .in2(SlotData[23:16]), .in3(SlotData[31:24]), .out(DataOut),
    .sel(Addr[1:0]), .en(Hit));
  assign Valid = L0 ? VALID_q : 1'bz;  // Controlled_Buffer controlled_buffer_1
  assign Valid = L1 ? VALID_2_q : 1'bz;  // Controlled_Buffer controlled_buffer_2
  assign Valid = L2 ? VALID_3_q : 1'bz;  // Controlled_Buffer controlled_buffer_3
  assign Valid = L3 ? VALID_4_q : 1'bz;  // Controlled_Buffer controlled_buffer_4
  assign Valid = L4 ? VALID_5_q : 1'bz;  // Controlled_Buffer controlled_buffer_5
  assign Valid = L5 ? VALID_6_q : 1'bz;  // Controlled_Buffer controlled_buffer_6
  assign Valid = L6 ? VALID_7_q : 1'bz;  // Controlled_Buffer controlled_buffer_7
  assign Valid = L7 ? VALID_8_q : 1'bz;  // Controlled_Buffer controlled_buffer_8
  Decoder #(.select(4), .tristate("false"), .disabled(0), .enable("false")) decoder_1 (
    .out0(L0), .out1(L1), .out2(L2), .out3(L3), .out4(L4), .out5(L5), .out6(L6), .out7(L7), .out8(L8),
    .out9(L9), .out10(L10), .out11(L11), .out12(L12), .out13(L13), .out14(L14), .out15(L15), .sel(Addr[5:2]));
  assign TagData = L0 ? TAG_q : 10'bz;  // Controlled_Buffer controlled_buffer_9
  Register #(.width(10), .trigger("rising"), .Select("low")) TAG (
    .D(Addr[15:6]), .en(and_2_out), .Q(TAG_q), .clk(CLK));  // open: clr
  Register #(.width(10), .trigger("rising"), .Select("low")) TAG_2 (
    .D(Addr[15:6]), .en(and_3_out), .Q(TAG_2_q), .clk(CLK));  // open: clr
  assign TagData = L1 ? TAG_2_q : 10'bz;  // Controlled_Buffer controlled_buffer_10
  Register #(.width(10), .trigger("rising"), .Select("low")) TAG_3 (
    .D(Addr[15:6]), .en(and_4_out), .Q(TAG_3_q), .clk(CLK));  // open: clr
  assign TagData = L2 ? TAG_3_q : 10'bz;  // Controlled_Buffer controlled_buffer_11
  assign TagData = L3 ? TAG_4_q : 10'bz;  // Controlled_Buffer controlled_buffer_12
  Register #(.width(10), .trigger("rising"), .Select("low")) TAG_4 (
    .D(Addr[15:6]), .en(and_5_out), .Q(TAG_4_q), .clk(CLK));  // open: clr
  assign TagData = L4 ? TAG_5_q : 10'bz;  // Controlled_Buffer controlled_buffer_13
  Register #(.width(10), .trigger("rising"), .Select("low")) TAG_5 (
    .D(Addr[15:6]), .en(and_6_out), .Q(TAG_5_q), .clk(CLK));  // open: clr
  Register #(.width(10), .trigger("rising"), .Select("low")) TAG_6 (
    .D(Addr[15:6]), .en(and_7_out), .Q(TAG_6_q), .clk(CLK));  // open: clr
  assign TagData = L5 ? TAG_6_q : 10'bz;  // Controlled_Buffer controlled_buffer_14
  Register #(.width(10), .trigger("rising"), .Select("low")) TAG_7 (
    .D(Addr[15:6]), .en(and_8_out), .Q(TAG_7_q), .clk(CLK));  // open: clr
  assign TagData = L6 ? TAG_7_q : 10'bz;  // Controlled_Buffer controlled_buffer_15
  assign TagData = L7 ? TAG_8_q : 10'bz;  // Controlled_Buffer controlled_buffer_16
  Register #(.width(10), .trigger("rising"), .Select("low")) TAG_8 (
    .D(Addr[15:6]), .en(and_9_out), .Q(TAG_8_q), .clk(CLK));  // open: clr
  Comparator #(.width(10), .mode("twosComplement")) comparator_1 (
    .a(Addr[15:6]), .b(TagData), .eq(comparator_1_eq));  // open: gt, lt
  Register #(.width(32), .trigger("rising"), .Select("low")) \u_数据块副本  (
    .D(BlockDataIn), .en(and_2_out), .Q(\数据块副本_q ), .clk(CLK));  // open: clr
  Register #(.width(32), .trigger("rising"), .Select("low")) DATA_COPY (
    .D(BlockDataIn), .en(and_3_out), .Q(DATA_COPY_q), .clk(CLK));  // open: clr
  Register #(.width(32), .trigger("rising"), .Select("low")) DATA_COPY_2 (
    .D(BlockDataIn), .en(and_4_out), .Q(DATA_COPY_2_q), .clk(CLK));  // open: clr
  Register #(.width(32), .trigger("rising"), .Select("low")) DATA_COPY_3 (
    .D(BlockDataIn), .en(and_5_out), .Q(DATA_COPY_3_q), .clk(CLK));  // open: clr
  Register #(.width(32), .trigger("rising"), .Select("low")) DATA_COPY_4 (
    .D(BlockDataIn), .en(and_6_out), .Q(DATA_COPY_4_q), .clk(CLK));  // open: clr
  Register #(.width(32), .trigger("rising"), .Select("low")) DATA_COPY_5 (
    .D(BlockDataIn), .en(and_7_out), .Q(DATA_COPY_5_q), .clk(CLK));  // open: clr
  Register #(.width(32), .trigger("rising"), .Select("low")) DATA_COPY_6 (
    .D(BlockDataIn), .en(and_8_out), .Q(DATA_COPY_6_q), .clk(CLK));  // open: clr
  Register #(.width(32), .trigger("rising"), .Select("low")) DATA_COPY_7 (
    .D(BlockDataIn), .en(and_9_out), .Q(DATA_COPY_7_q), .clk(CLK));  // open: clr
  and and_1 (Hit, comparator_1_eq, Valid);
  assign SlotData = L0 ? \数据块副本_q  : 32'bz;  // Controlled_Buffer controlled_buffer_17
  assign SlotData = L1 ? DATA_COPY_q : 32'bz;  // Controlled_Buffer controlled_buffer_18
  assign SlotData = L2 ? DATA_COPY_2_q : 32'bz;  // Controlled_Buffer controlled_buffer_19
  assign SlotData = L3 ? DATA_COPY_3_q : 32'bz;  // Controlled_Buffer controlled_buffer_20
  assign SlotData = L4 ? DATA_COPY_4_q : 32'bz;  // Controlled_Buffer controlled_buffer_21
  assign SlotData = L5 ? DATA_COPY_5_q : 32'bz;  // Controlled_Buffer controlled_buffer_22
  assign SlotData = L6 ? DATA_COPY_6_q : 32'bz;  // Controlled_Buffer controlled_buffer_23
  assign SlotData = L7 ? DATA_COPY_7_q : 32'bz;  // Controlled_Buffer controlled_buffer_24
  not not_1 (Miss, Hit);
  and and_2 (and_2_out, L0, BlkDataReady);
  and and_3 (and_3_out, L1, BlkDataReady);
  and and_4 (and_4_out, L2, BlkDataReady);
  and and_5 (and_5_out, L3, BlkDataReady);
  and and_6 (and_6_out, L4, BlkDataReady);
  and and_7 (and_7_out, L5, BlkDataReady);
  and and_8 (and_8_out, L6, BlkDataReady);
  and and_9 (and_9_out, L7, BlkDataReady);
  Register #(.width(1), .trigger("rising"), .Select("low")) VALID_9 (
    .D(1'b1), .en(and_10_out), .Q(VALID_9_q), .clk(CLK));  // open: clr
  Register #(.width(1), .trigger("rising"), .Select("low")) VALID_10 (
    .D(1'b1), .en(and_11_out), .Q(VALID_10_q), .clk(CLK));  // open: clr
  Register #(.width(1), .trigger("rising"), .Select("low")) VALID_11 (
    .D(1'b1), .en(and_12_out), .Q(VALID_11_q), .clk(CLK));  // open: clr
  Register #(.width(1), .trigger("rising"), .Select("low")) VALID_12 (
    .D(1'b1), .en(and_13_out), .Q(VALID_12_q), .clk(CLK));  // open: clr
  Register #(.width(1), .trigger("rising"), .Select("low")) VALID_13 (
    .D(1'b1), .en(and_14_out), .Q(VALID_13_q), .clk(CLK));  // open: clr
  Register #(.width(1), .trigger("rising"), .Select("low")) VALID_14 (
    .D(1'b1), .en(and_15_out), .Q(VALID_14_q), .clk(CLK));  // open: clr
  Register #(.width(1), .trigger("rising"), .Select("low")) VALID_15 (
    .D(1'b1), .en(and_16_out), .Q(VALID_15_q), .clk(CLK));  // open: clr
  Register #(.width(1), .trigger("rising"), .Select("low")) VALID_16 (
    .D(1'b1), .en(and_17_out), .Q(VALID_16_q), .clk(CLK));  // open: clr
  assign Valid = L8 ? VALID_9_q : 1'bz;  // Controlled_Buffer controlled_buffer_25
  assign Valid = L9 ? VALID_10_q : 1'bz;  // Controlled_Buffer controlled_buffer_26
  assign Valid = L10 ? VALID_11_q : 1'bz;  // Controlled_Buffer controlled_buffer_27
  assign Valid = L11 ? VALID_12_q : 1'bz;  // Controlled_Buffer controlled_buffer_28
  assign Valid = L12 ? VALID_13_q : 1'bz;  // Controlled_Buffer controlled_buffer_29
  assign Valid = L13 ? VALID_14_q : 1'bz;  // Controlled_Buffer controlled_buffer_30
  assign Valid = L14 ? VALID_15_q : 1'bz;  // Controlled_Buffer controlled_buffer_31
  assign Valid = L15 ? VALID_16_q : 1'bz;  // Controlled_Buffer controlled_buffer_32
  assign TagData = L8 ? TAG_9_q : 10'bz;  // Controlled_Buffer controlled_buffer_33
  Register #(.width(10), .trigger("rising"), .Select("low")) TAG_9 (
    .D(Addr[15:6]), .en(and_10_out), .Q(TAG_9_q), .clk(CLK));  // open: clr
  Register #(.width(10), .trigger("rising"), .Select("low")) TAG_10 (
    .D(Addr[15:6]), .en(and_11_out), .Q(TAG_10_q), .clk(CLK));  // open: clr
  assign TagData = L9 ? TAG_10_q : 10'bz;  // Controlled_Buffer controlled_buffer_34
  Register #(.width(10), .trigger("rising"), .Select("low")) TAG_11 (
    .D(Addr[15:6]), .en(and_12_out), .Q(TAG_11_q), .clk(CLK));  // open: clr
  assign TagData = L10 ? TAG_11_q : 10'bz;  // Controlled_Buffer controlled_buffer_35
  Register #(.width(10), .trigger("rising"), .Select("low")) TAG_12 (
    .D(Addr[15:6]), .en(and_13_out), .Q(TAG_12_q), .clk(CLK));  // open: clr
  assign TagData = L11 ? TAG_12_q : 10'bz;  // Controlled_Buffer controlled_buffer_36
  Register #(.width(10), .trigger("rising"), .Select("low")) TAG_13 (
    .D(Addr[15:6]), .en(and_14_out), .Q(TAG_13_q), .clk(CLK));  // open: clr
  assign TagData = L12 ? TAG_13_q : 10'bz;  // Controlled_Buffer controlled_buffer_37
  Register #(.width(10), .trigger("rising"), .Select("low")) TAG_14 (
    .D(Addr[15:6]), .en(and_15_out), .Q(TAG_14_q), .clk(CLK));  // open: clr
  assign TagData = L13 ? TAG_14_q : 10'bz;  // Controlled_Buffer controlled_buffer_38
  Register #(.width(10), .trigger("rising"), .Select("low")) TAG_15 (
    .D(Addr[15:6]), .en(and_16_out), .Q(TAG_15_q), .clk(CLK));  // open: clr
  assign TagData = L14 ? TAG_15_q : 10'bz;  // Controlled_Buffer controlled_buffer_39
  Register #(.width(10), .trigger("rising"), .Select("low")) TAG_16 (
    .D(Addr[15:6]), .en(and_17_out), .Q(TAG_16_q), .clk(CLK));  // open: clr
  assign TagData = L15 ? TAG_16_q : 10'bz;  // Controlled_Buffer controlled_buffer_40
  Register #(.width(32), .trigger("rising"), .Select("low")) \u_数据块副本_2  (
    .D(BlockDataIn), .en(and_10_out), .Q(\数据块副本_2_q ), .clk(CLK));  // open: clr
  Register #(.width(32), .trigger("rising"), .Select("low")) DATA_COPY_8 (
    .D(BlockDataIn), .en(and_11_out), .Q(DATA_COPY_8_q), .clk(CLK));  // open: clr
  Register #(.width(32), .trigger("rising"), .Select("low")) DATA_COPY_9 (
    .D(BlockDataIn), .en(and_12_out), .Q(DATA_COPY_9_q), .clk(CLK));  // open: clr
  Register #(.width(32), .trigger("rising"), .Select("low")) DATA_COPY_10 (
    .D(BlockDataIn), .en(and_13_out), .Q(DATA_COPY_10_q), .clk(CLK));  // open: clr
  Register #(.width(32), .trigger("rising"), .Select("low")) DATA_COPY_11 (
    .D(BlockDataIn), .en(and_14_out), .Q(DATA_COPY_11_q), .clk(CLK));  // open: clr
  Register #(.width(32), .trigger("rising"), .Select("low")) DATA_COPY_12 (
    .D(BlockDataIn), .en(and_15_out), .Q(DATA_COPY_12_q), .clk(CLK));  // open: clr
  Register #(.width(32), .trigger("rising"), .Select("low")) DATA_COPY_13 (
    .D(BlockDataIn), .en(and_16_out), .Q(DATA_COPY_13_q), .clk(CLK));  // open: clr
  Register #(.width(32), .trigger("rising"), .Select("low")) DATA_COPY_14 (
    .D(BlockDataIn), .en(and_17_out), .Q(DATA_COPY_14_q), .clk(CLK));  // open: clr
  assign SlotData = L8 ? \数据块副本_2_q  : 32'bz;  // Controlled_Buffer controlled_buffer_41
  assign SlotData = L9 ? DATA_COPY_8_q : 32'bz;  // Controlled_Buffer controlled_buffer_42
  assign SlotData = L10 ? DATA_COPY_9_q : 32'bz;  // Controlled_Buffer controlled_buffer_43
  assign SlotData = L11 ? DATA_COPY_10_q : 32'bz;  // Controlled_Buffer controlled_buffer_44
  assign SlotData = L12 ? DATA_COPY_11_q : 32'bz;  // Controlled_Buffer controlled_buffer_45
  assign SlotData = L13 ? DATA_COPY_12_q : 32'bz;  // Controlled_Buffer controlled_buffer_46
  assign SlotData = L14 ? DATA_COPY_13_q : 32'bz;  // Controlled_Buffer controlled_buffer_47
  assign SlotData = L15 ? DATA_COPY_14_q : 32'bz;  // Controlled_Buffer controlled_buffer_48
  and and_10 (and_10_out, L8, BlkDataReady);
  and and_11 (and_11_out, L9, BlkDataReady);
  and and_12 (and_12_out, L10, BlkDataReady);
  and and_13 (and_13_out, L11, BlkDataReady);
  and and_14 (and_14_out, L12, BlkDataReady);
  and and_15 (and_15_out, L13, BlkDataReady);
  and and_16 (and_16_out, L14, BlkDataReady);
  and and_17 (and_17_out, L15, BlkDataReady);

  // Other names for the same wires on the sheet: Blk[31:0] = BlockDataIn; BlkReady = BlkDataReady;
  //   Offset[1:0] = Addr[1:0]; 字节地址[15:0] = Addr; Index[3:0] = Addr[5:2]; Tag[9:0] = Addr[15:6]

  // Notes on the sheet:
  //   输入引脚区
  //   有效位
  //   三态门控制多行输出
  //   行选中
  //   标记位
  //   cache（直接相联映射）电路（16个cache块）
  //   块数据输出
  //   输出引脚区
  //   有效位
  //   三态门控制多行输出
  //   行选中
  //   标记位
  //   块数据输出
endmodule

// 全相联cache
module \cache_全相联映射_电路_4个cache块  (
  input  BlkDataReady,
  input  [15:0] Addr,
  input  [31:0] BlockDataIn,
  input  CLK,
  output Miss,
  output [7:0] DataOut
);


  // Other names for the same wires on the sheet: Blk[31:0] = BlockDataIn; BlkReady = BlkDataReady; 字节地址[15:0] = Addr

  // Notes on the sheet:
  //   输入引脚区
  //   cache（全相联映射）电路（4个cache块）
  //   请同学们在此设计电路！
  //   输出引脚区
endmodule

// 全相联cache
module \cache_全相联映射_电路_16个cache块  (
  input  BlkDataReady,
  input  [15:0] Addr,
  input  [31:0] BlockDataIn,
  input  CLK,
  output Miss,
  output [7:0] DataOut
);


  // Other names for the same wires on the sheet: Blk[31:0] = BlockDataIn; BlkReady = BlkDataReady; 字节地址[15:0] = Addr

  // Notes on the sheet:
  //   输入引脚区
  //   cache（全相联映射）电路（16个cache块）
  //   请同学们在此设计电路！
  //   输出引脚区
endmodule

// 2路组相联cache
module \cache_2路组相联映射_电路_4个cache块  (
  input  BlkDataReady,
  input  [15:0] Addr,
  input  [31:0] BlockDataIn,
  input  CLK,
  output Miss,
  output [7:0] DataOut
);


  // Other names for the same wires on the sheet: Blk[31:0] = BlockDataIn; BlkReady = BlkDataReady; 字节地址[15:0] = Addr

  // Notes on the sheet:
  //   输入引脚区
  //   cache（2路组相联映射）电路（4个cache块）
  //   请同学们在此设计电路！
  //   输出引脚区
endmodule

// 2路组相联cache
module \cache_2路组相联_电路_16个cache块  (
  input  BlkDataReady,
  input  [15:0] Addr,
  input  [31:0] BlockDataIn,
  input  CLK,
  output Miss,
  output [7:0] DataOut
);


  // Other names for the same wires on the sheet: Blk[31:0] = BlockDataIn; BlkReady = BlkDataReady; 字节地址[15:0] = Addr

  // Notes on the sheet:
  //   输入引脚区
  //   cache（2路组相联映射）电路（16个cache块）
  //   请同学们在此设计电路！
  //   输出引脚区
endmodule

// 4路组相联cache
module \cache_4路组相联映射_电路_16个cache块  (
  input  BlkDataReady,
  input  [31:0] BlockDataIn,
  input  [15:0] Addr,
  input  CLK,
  output Miss,
  output [7:0] DataOut
);


  // Other names for the same wires on the sheet: Blk[31:0] = BlockDataIn; BlkReady = BlkDataReady; 字节地址[15:0] = Addr

  // Notes on the sheet:
  //   输入引脚区
  //   cache（4路组相联映射）电路（16个cache块）
  //   请同学们在此设计电路！
  //   输出引脚区
endmodule

// 8路组相联cache
module \cache_8路组相联映射_电路_16个cache块  (
  input  BlkDataReady,
  input  [31:0] BlockDataIn,
  input  [15:0] Addr,
  input  CLK,
  output Miss,
  output [7:0] DataOut
);


  // Other names for the same wires on the sheet: Blk[31:0] = BlockDataIn; BlkReady = BlkDataReady; 字节地址[15:0] = Addr

  // Notes on the sheet:
  //   输入引脚区
  //   cache（8路组相联映射）电路（16个cache块）
  //   请同学们在此设计电路！
  //   输出引脚区
endmodule
