// Logisim project 32位快速加法器（组内并行，组间并行）.circ as structural Verilog: 6 circuits, main circuit 4位先行进位电路
module \_4位先行进位电路  (
  input  G4,
  input  P4,
  input  G3,
  input  P3,
  input  G2,
  input  P2,
  input  G1,
  input  P1,
  input  Cin,
  output C4,
  output C3,
  output C2,
  output C1,
  output G_star,
  output P_star
);

  wire and_2_out, and_3_out, and_4_out, and_5_out, and_6_out, and_7_out, and_8_out, and_9_out, and_10_out,
       and_11_out;

  and and_1 (P_star, P4, P3, P2, P1);
  or or_1 (G_star, G4, and_3_out, and_2_out, and_4_out);
  and and_2 (and_2_out, P4, P3, G2);
  and and_3 (and_3_out, P4, G3);
  or or_2 (C4, G4, and_3_out, and_2_out, and_4_out, and_5_out);
  and and_4 (and_4_out, P4, P3, P2, G1);
  and and_5 (and_5_out, P4, P3, P2, P1, Cin);
  or or_3 (C3, G3, and_6_out, and_8_out, and_7_out);
  and and_6 (and_6_out, P3, G2);
  and and_7 (and_7_out, P3, P2, P1, Cin);
  and and_8 (and_8_out, P3, P2, G1);
  or or_4 (C2, G2, and_9_out, and_10_out);
  and and_9 (and_9_out, P2, G1);
  and and_10 (and_10_out, P2, P1, Cin);
  or or_5 (C1, G1, and_11_out);
  and and_11 (and_11_out, P1, Cin);

  // Notes on the sheet:
  //   Cin: pull=down
  //   P4: pull=down
  //   G4: pull=down
  //   G2: pull=down
  //   P2: pull=down
  //   G1: pull=down
  //   P1: pull=down
  //   G3: pull=down
  //   P3: pull=down
  //   输入引脚区
  //   4位先行进位电路
  //   输出引脚区
endmodule

module \_4位快速加法器  (
  input  [3:0] X,
  input  [3:0] Y,
  input  C0,
  output [3:0] S,
  output C4,
  output C3,
  output OF,
  output G_star,
  output P_star
);

  wire and_1_out, and_2_out, and_3_out, and_4_out, \n4位先行进位电路_1_c1 , \n4位先行进位电路_1_c2 , T0, T1, T2, T3;

  xor xor_1 (OF, C3, C4);
  \_4位先行进位电路  \u_4位先行进位电路_1  (
    .G4(and_1_out), .P4(T3), .G3(and_2_out), .P3(T2), .G2(and_3_out), .P2(T1), .G1(and_4_out), .P1(T0),
    .Cin(C0), .C4(C4), .C3(C3), .C2(\n4位先行进位电路_1_c2 ), .C1(\n4位先行进位电路_1_c1 ), .G_star(G_star), .P_star(P_star));
  and and_1 (and_1_out, X[3], Y[3]);
  xor xor_2 (S[3], C3, T3);
  xor xor_3 (T3, X[3], Y[3]);
  xor xor_4 (T2, X[2], Y[2]);
  and and_2 (and_2_out, X[2], Y[2]);
  xor xor_5 (S[2], \n4位先行进位电路_1_c2 , T2);
  and and_3 (and_3_out, X[1], Y[1]);
  xor xor_6 (T1, X[1], Y[1]);
  xor xor_7 (S[1], \n4位先行进位电路_1_c1 , T1);
  and and_4 (and_4_out, X[0], Y[0]);
  // Probe on X
  // Probe on Y
  // Probe on S
  xor xor_8 (S[0], T0, C0);
  xor xor_9 (T0, X[0], Y[0]);
  // Probe on X
  // Probe on Y
  // Probe on S

  // Notes on the sheet:
  //   C0: pull=down
  //   X: pull=down
  //   Y: pull=down
  //   输入引脚区
  //   输出引脚区
  //   功能说明：4位快速加法器            输入：X、Y、C0           输出：S、C4、C3、OF、G*、P*          C3为最高数据位的进位，G*、P*为成组进位生成传递函数
  //   4位快速加法器
  //   +
  //   =
  //   有符号加法
  //   +
  //   =
  //   无符号加法
endmodule

module \_16位快速加法器_组内并行_组间串行  (
  input  [15:0] X,
  input  [15:0] Y,
  input  C0,
  output C16,
  output C15,
  output OF,
  output [15:0] S
);

  wire \n4位快速加法器_2_c4 , \n4位快速加法器_3_c4 , \n4位快速加法器_4_c4 ;

  xor xor_1 (OF, C16, C15);
  \_4位快速加法器  \u_4位快速加法器_1  (
    .X(X[15:12]), .Y(Y[15:12]), .C0(\n4位快速加法器_2_c4 ), .S(S[15:12]), .C4(C16), .C3(C15));  // open: OF, G_star, P_star
  \_4位快速加法器  \u_4位快速加法器_2  (
    .X(X[11:8]), .Y(Y[11:8]), .C0(\n4位快速加法器_3_c4 ), .S(S[11:8]), .C4(\n4位快速加法器_2_c4 ));  // open: OF, G_star, C3, P_star
  \_4位快速加法器  \u_4位快速加法器_3  (
    .X(X[7:4]), .Y(Y[7:4]), .C0(\n4位快速加法器_4_c4 ), .S(S[7:4]), .C4(\n4位快速加法器_3_c4 ));  // open: OF, G_star, C3, P_star
  // Probe on X
  // Probe on Y
  // Probe on S
  \_4位快速加法器  \u_4位快速加法器_4  (
    .X(X[3:0]), .Y(Y[3:0]), .C0(C0), .S(S[3:0]), .C4(\n4位快速加法器_4_c4 ));  // open: OF, G_star, C3, P_star
  // Probe on X
  // Probe on Y
  // Probe on S

  // Other names for the same wires on the sheet: S0[3:0] = S[3:0]; S1[3:0] = S[7:4]; S2[3:0] = S[11:8];
  //   S3[3:0] = S[15:12]; X0[3:0] = X[3:0]; X1[3:0] = X[7:4]; X2[3:0] = X[11:8]; X3[3:0] = X[15:12]; Y0[3:0] = Y[3:0];
  //   Y1[3:0] = Y[7:4]; Y2[3:0] = Y[11:8]; Y3[3:0] = Y[15:12]

  // Notes on the sheet:
  //   C0: pull=down
  //   Y: pull=down
  //   X: pull=down
  //   输入引脚区
  //   输出引脚区
  //   功能说明：16位快速加法器       输入：X、Y、C0        输出：S、C16、C15（最高数据位的进位）、OF（溢出标志）       
  //   16位快速加法器（组内并行、组间串行）
  //   +
  //   =
  //   有符号加法
  //   +
  //   =
  //   无符号加法
endmodule

module \_16位快速加法器_组内并行_组间并行  (
  input  [15:0] X,
  input  [15:0] Y,
  input  C0,
  output C16,
  output C15,
  output OF,
  output G_star,
  output P_star,
  output [15:0] S
);

  wire and_2_out, and_3_out, and_4_out, and_5_out, and_6_out, and_7_out, and_8_out, and_9_out, and_10_out,
       and_11_out, \n4位快速加法器_1_g_star , \n4位快速加法器_1_p_star , \n4位快速加法器_2_g_star , \n4位快速加法器_2_p_star ,
       \n4位快速加法器_3_g_star , \n4位快速加法器_3_p_star , \n4位快速加法器_4_g_star , \n4位快速加法器_4_p_star , or_3_out,
       or_4_out, or_5_out;

  xor xor_1 (OF, C16, C15);
  and and_1 (P_star, \n4位快速加法器_1_p_star , \n4位快速加法器_2_p_star , \n4位快速加法器_3_p_star , \n4位快速加法器_4_p_star );
  or or_1 (G_star, and_4_out, and_2_out, and_3_out, \n4位快速加法器_1_g_star );
  and and_2 (and_2_out, \n4位快速加法器_1_p_star , \n4位快速加法器_2_p_star , \n4位快速加法器_3_g_star );
  and and_3 (and_3_out, \n4位快速加法器_1_p_star , \n4位快速加法器_2_g_star );
  or or_2 (C16, \n4位快速加法器_1_g_star , and_3_out, and_2_out, and_4_out, and_5_out);
  and and_4 (and_4_out, \n4位快速加法器_1_p_star , \n4位快速加法器_2_p_star , \n4位快速加法器_3_p_star , \n4位快速加法器_4_g_star );
  and and_5 (and_5_out, \n4位快速加法器_1_p_star , \n4位快速加法器_2_p_star , \n4位快速加法器_3_p_star , \n4位快速加法器_4_p_star , C0);
  \_4位快速加法器  \u_4位快速加法器_1  (
    .X(X[15:12]), .Y(Y[15:12]), .C0(or_3_out), .S(S[15:12]), .G_star(\n4位快速加法器_1_g_star ), .C3(C15),
    .P_star(\n4位快速加法器_1_p_star ));  // open: C4, OF
  // Probe on X
  // Probe on Y
  // Probe on S
  or or_3 (or_3_out, \n4位快速加法器_2_g_star , and_7_out, and_6_out, and_8_out);
  and and_6 (and_6_out, \n4位快速加法器_2_p_star , \n4位快速加法器_3_p_star , \n4位快速加法器_4_g_star );
  and and_7 (and_7_out, \n4位快速加法器_2_p_star , \n4位快速加法器_3_g_star );
  and and_8 (and_8_out, \n4位快速加法器_2_p_star , \n4位快速加法器_3_p_star , \n4位快速加法器_4_p_star , C0);
  \_4位快速加法器  \u_4位快速加法器_2  (
    .X(X[11:8]), .Y(Y[11:8]), .C0(or_4_out), .S(S[11:8]), .G_star(\n4位快速加法器_2_g_star ),
    .P_star(\n4位快速加法器_2_p_star ));  // open: C4, OF, C3
  // Probe on X
  // Probe on Y
  // Probe on S
  or or_4 (or_4_out, \n4位快速加法器_3_g_star , and_10_out, and_9_out);
  and and_9 (and_9_out, \n4位快速加法器_3_p_star , \n4位快速加法器_4_p_star , C0);
  and and_10 (and_10_out, \n4位快速加法器_3_p_star , \n4位快速加法器_4_g_star );
  \_4位快速加法器  \u_4位快速加法器_3  (
    .X(X[7:4]), .Y(Y[7:4]), .C0(or_5_out), .S(S[7:4]), .G_star(\n4位快速加法器_3_g_star ),
    .P_star(\n4位快速加法器_3_p_star ));  // open: C4, OF, C3
  or or_5 (or_5_out, \n4位快速加法器_4_g_star , and_11_out);
  and and_11 (and_11_out, \n4位快速加法器_4_p_star , C0);
  \_4位快速加法器  \u_4位快速加法器_4  (
    .X(X[3:0]), .Y(Y[3:0]), .C0(C0), .S(S[3:0]), .G_star(\n4位快速加法器_4_g_star ), .P_star(\n4位快速加法器_4_p_star ));  // open: C4, OF, C3

  // Other names for the same wires on the sheet: S0[3:0] = S[3:0]; S1[3:0] = S[7:4]; S2[3:0] = S[11:8];
  //   S3[3:0] = S[15:12]; X0[3:0] = X[3:0]; X1[3:0] = X[7:4]; X2[3:0] = X[11:8]; X3[3:0] = X[15:12]; Y0[3:0] = Y[3:0];
  //   Y1[3:0] = Y[7:4]; Y2[3:0] = Y[11:8]; Y3[3:0] = Y[15:12]

  // Notes on the sheet:
  //   C0: pull=down
  //   Y: pull=down
  //   X: pull=down
  //   输入引脚区
  //   输出引脚区
  //   功能说明：16位快速加法器               输入：X、Y、C0                输出：S、C16、C15（最高数据位的进位）、OF、G*、P*       
  //   16位快速加法器（组内并行、组间并行）
  //   +
  //   =
  //   有符号加法
  //   +
  //   =
  //   无符号加法
endmodule

module \_32位快速加法器_组内并行_组间串行__1  (
  input  [31:0] X,
  input  [31:0] Y,
  input  C0,
  output C32,
  output C31,
  output OF,
  output [31:0] S
);

  wire \n16位快速加法器_组内并行_组间串行_2_c16 ;

  xor xor_1 (OF, C32, C31);
  \_16位快速加法器_组内并行_组间串行  \u_16位快速加法器_组内并行_组间串行_1  (
    .X(X[31:16]), .Y(Y[31:16]), .C0(\n16位快速加法器_组内并行_组间串行_2_c16 ), .S(S[31:16]), .C16(C32), .C15(C31));  // open: OF
  // Probe on X
  // Probe on Y
  // Probe on S
  \_16位快速加法器_组内并行_组间串行  \u_16位快速加法器_组内并行_组间串行_2  (
    .X(X[15:0]), .Y(Y[15:0]), .C0(C0), .S(S[15:0]), .C16(\n16位快速加法器_组内并行_组间串行_2_c16 ));  // open: C15, OF
  // Probe on X
  // Probe on Y
  // Probe on S

  // Other names for the same wires on the sheet: S0[15:0] = S[15:0]; S1[15:0] = S[31:16]; X0[15:0] = X[15:0];
  //   X1[15:0] = X[31:16]; Y0[15:0] = Y[15:0]; Y1[15:0] = Y[31:16]

  // Notes on the sheet:
  //   Y: pull=down
  //   C0: pull=down
  //   X: pull=down
  //   输入引脚区
  //   输出引脚区
  //   功能说明：32位快速加法器               输入：X、Y、C0                输出：S、C32、C31（最高数据位的进位）、OF      
  //   32位快速加法器（组内并行、组间串行）
  //   +
  //   =
  //   有符号加法
  //   +
  //   =
  //   无符号加法
  //   （16位加法器采用：组内并行、组间串行）
endmodule

module \_32位快速加法器_组内并行_组间串行__2  (
  input  [31:0] X,
  input  [31:0] Y,
  input  C0,
  output C32,
  output C31,
  output OF,
  output [31:0] S
);

  wire \n16位快速加法器_组内并行_组间并行_2_c16 ;

  xor xor_1 (OF, C32, C31);
  \_16位快速加法器_组内并行_组间并行  \u_16位快速加法器_组内并行_组间并行_1  (
    .X(X[31:16]), .Y(Y[31:16]), .C0(\n16位快速加法器_组内并行_组间并行_2_c16 ), .S(S[31:16]), .C16(C32), .C15(C31));  // open: OF, G_star, P_star
  // Probe on X
  // Probe on Y
  // Probe on S
  \_16位快速加法器_组内并行_组间并行  \u_16位快速加法器_组内并行_组间并行_2  (
    .X(X[15:0]), .Y(Y[15:0]), .C0(C0), .S(S[15:0]), .C16(\n16位快速加法器_组内并行_组间并行_2_c16 ));  // open: C15, OF, G_star, P_star
  // Probe on X
  // Probe on Y
  // Probe on S

  // Other names for the same wires on the sheet: S0[15:0] = S[15:0]; S1[15:0] = S[31:16]; X0[15:0] = X[15:0];
  //   X1[15:0] = X[31:16]; Y0[15:0] = Y[15:0]; Y1[15:0] = Y[31:16]

  // Notes on the sheet:
  //   C0: pull=down
  //   X: pull=down
  //   Y: pull=down
  //   输入引脚区
  //   32位快速加法器（组内并行、组间串行）
  //   输出引脚区
  //   功能说明：32位快速加法器               输入：X、Y、C0                输出：S、C32、C31（最高数据位的进位）、OF      
  //   +
  //   =
  //   有符号加法
  //   （16位加法器采用：组内并行、组间并行）
  //   +
  //   =
  //   无符号加法
endmodule
